// Logisim project CSA 2.circ as structural Verilog: 5 circuits, main circuit Full Adder
module Full_Adder (
  input  A,
  input  B,
  input  CarryIn,
  output SUM,
  output CarryOut
);

  wire and_1_out, and_2_out, and_3_out, and_4_out, and_5_out, and_6_out, and_7_out, not_1_out, not_2_out,
       not_3_out;

  not not_1 (not_1_out, A);
  not not_2 (not_2_out, B);
  not not_3 (not_3_out, CarryIn);
  and and_1 (and_1_out, not_1_out, not_2_out, CarryIn);
  and and_2 (and_2_out, not_1_out, B, not_3_out);
  and and_3 (and_3_out, A, not_2_out, not_3_out);
  and and_4 (and_4_out, A, B, CarryIn);
  and and_5 (and_5_out, B, CarryIn);
  and and_6 (and_6_out, A, CarryIn);
  and and_7 (and_7_out, A, B);
  or or_1 (SUM, and_1_out, and_2_out, and_3_out, and_4_out);
  or or_2 (CarryOut, and_5_out, and_6_out, and_7_out);
endmodule

module Ripple_Carry_Adder (
  input  Cin,
  input  [15:0] A,
  input  [15:0] B,
  output [15:0] SUM,
  output out_5
);

  wire full_adder_1_carryout, full_adder_2_carryout, full_adder_3_carryout, full_adder_4_carryout,
       full_adder_5_carryout, full_adder_6_carryout, full_adder_7_carryout, full_adder_8_carryout,
       full_adder_9_carryout, full_adder_10_carryout, full_adder_11_carryout, full_adder_12_carryout,
       full_adder_13_carryout, full_adder_14_carryout, LSB_carryout, MSB_carryout;

  Full_Adder LSB (.A(A[0]), .B(B[0]), .CarryIn(Cin), .SUM(SUM[0]), .CarryOut(LSB_carryout));
  Full_Adder full_adder_1 (.A(A[1]), .B(B[1]), .CarryIn(LSB_carryout), .SUM(SUM[1]), .CarryOut(full_adder_1_carryout));
  Full_Adder full_adder_2 (
    .A(A[2]), .B(B[2]), .CarryIn(full_adder_1_carryout), .SUM(SUM[2]), .CarryOut(full_adder_2_carryout));
  Full_Adder full_adder_3 (
    .A(A[3]), .B(B[3]), .CarryIn(full_adder_2_carryout), .SUM(SUM[3]), .CarryOut(full_adder_3_carryout));
  Full_Adder full_adder_4 (
    .A(A[4]), .B(B[4]), .CarryIn(full_adder_3_carryout), .SUM(SUM[4]), .CarryOut(full_adder_4_carryout));
  Full_Adder full_adder_5 (
    .A(A[5]), .B(B[5]), .CarryIn(full_adder_4_carryout), .SUM(SUM[5]), .CarryOut(full_adder_5_carryout));
  Full_Adder full_adder_6 (
    .A(A[6]), .B(B[6]), .CarryIn(full_adder_5_carryout), .SUM(SUM[6]), .CarryOut(full_adder_6_carryout));
  Full_Adder full_adder_7 (
    .A(A[7]), .B(B[7]), .CarryIn(full_adder_6_carryout), .SUM(SUM[7]), .CarryOut(full_adder_7_carryout));
  Full_Adder full_adder_8 (
    .A(A[8]), .B(B[8]), .CarryIn(full_adder_7_carryout), .SUM(SUM[8]), .CarryOut(full_adder_8_carryout));
  Full_Adder full_adder_9 (
    .A(A[9]), .B(B[9]), .CarryIn(full_adder_8_carryout), .SUM(SUM[9]), .CarryOut(full_adder_9_carryout));
  Full_Adder full_adder_10 (
    .A(A[10]), .B(B[10]), .CarryIn(full_adder_9_carryout), .SUM(SUM[10]), .CarryOut(full_adder_10_carryout));
  Full_Adder full_adder_11 (
    .A(A[11]), .B(B[11]), .CarryIn(full_adder_10_carryout), .SUM(SUM[11]), .CarryOut(full_adder_11_carryout));
  Full_Adder full_adder_12 (
    .A(A[12]), .B(B[12]), .CarryIn(full_adder_11_carryout), .SUM(SUM[12]), .CarryOut(full_adder_12_carryout));
  Full_Adder full_adder_13 (
    .A(A[13]), .B(B[13]), .CarryIn(full_adder_12_carryout), .SUM(SUM[13]), .CarryOut(full_adder_13_carryout));
  Full_Adder full_adder_14 (
    .A(A[14]), .B(B[14]), .CarryIn(full_adder_13_carryout), .SUM(SUM[14]), .CarryOut(full_adder_14_carryout));
  Full_Adder MSB (.A(A[15]), .B(B[15]), .CarryIn(full_adder_14_carryout), .SUM(SUM[15]), .CarryOut(MSB_carryout));
  xor xor_1 (out_5, full_adder_14_carryout, MSB_carryout);
endmodule

module _4_bit_adder (
  input  Carryin,
  input  a0,
  input  a1,
  input  a2,
  input  a3,
  input  b0,
  input  b1,
  input  b2,
  input  b3,
  output s0,
  output s1,
  output s2,
  output s3,
  output Overflow,
  output P0,
  output G0
);

  wire and_2_out, and_3_out, and_4_out, c1_out, c2_out, c3_out, c4_out, g0_out, g1_out, g2_out, g3_out,
       p0_out, p0c0_out, p1_out, p1g0_out, p1p0c0_out, p2_out, p2g1_out, p2p1g0_out, p2p1p0c0_out, p3_out,
       p3g2_out, p3p2g1_out, p3p2p1g0_out, p3p2p1p0c0_out;

  and u_g0 (g0_out, a0, b0);
  or u_p0 (p0_out, a0, b0);
  and g1 (g1_out, a1, b1);
  or p1 (p1_out, a1, b1);
  and g2 (g2_out, a2, b2);
  or p2 (p2_out, a2, b2);
  and g3 (g3_out, a3, b3);
  or p3 (p3_out, a3, b3);
  and p0c0 (p0c0_out, Carryin, p0_out);
  and p1p0c0 (p1p0c0_out, p1_out, p0_out, Carryin);
  and p1g0 (p1g0_out, g0_out, p1_out);
  and p2g1 (p2g1_out, p2_out, g1_out);
  and p2p1g0 (p2p1g0_out, p2_out, p1_out, g0_out);
  and p2p1p0c0 (p2p1p0c0_out, p2_out, p1_out, p0_out, Carryin);
  and p3g2 (p3g2_out, p3_out, g2_out);
  and p3p2g1 (p3p2g1_out, p3_out, p2_out, g1_out);
  and p3p2p1g0 (p3p2p1g0_out, p3_out, p2_out, p1_out, g0_out);
  and p3p2p1p0c0 (p3p2p1p0c0_out, p3_out, p2_out, p1_out, p0_out, Carryin);
  or c1 (c1_out, g0_out, p0c0_out);
  or c2 (c2_out, g1_out, p1p0c0_out, p1g0_out);
  or c3 (c3_out, g2_out, p2g1_out, p2p1g0_out, p2p1p0c0_out);
  Full_Adder full_adder_1 (.A(a0), .B(b0), .CarryIn(Carryin), .SUM(s0));  // open: CarryOut
  Full_Adder full_adder_2 (.A(a1), .B(b1), .CarryIn(c1_out), .SUM(s1));  // open: CarryOut
  Full_Adder full_adder_3 (.A(a2), .B(b2), .CarryIn(c2_out), .SUM(s2));  // open: CarryOut
  Full_Adder full_adder_4 (.A(a3), .B(b3), .CarryIn(c3_out), .SUM(s3));  // open: CarryOut
  or c4 (c4_out, g3_out, p3g2_out, p3p2g1_out, p3p2p1g0_out, p3p2p1p0c0_out);
  xor xor_1 (Overflow, c3_out, c4_out);
  and and_1 (P0, p0_out, p1_out, p2_out, p3_out);
  and and_2 (and_2_out, p3_out, g2_out);
  and and_3 (and_3_out, p3_out, p2_out, g1_out);
  and and_4 (and_4_out, p3_out, p2_out, p1_out, p1_out, g0_out);
  or or_1 (G0, and_2_out, and_3_out, and_4_out, g3_out);
endmodule

module _12_bit_adder_carry_lookahead (
  input  CarryIn,
  input  [15:0] a,
  input  [15:0] b,
  output [15:0] SUM,
  output Overflow
);

  wire C1_out, C2_out, C3_out, n4_bit_adder_1_g0, n4_bit_adder_1_p0, n4_bit_adder_2_g0, n4_bit_adder_2_p0,
       n4_bit_adder_3_g0, n4_bit_adder_3_p0, P0c0_out, P1G0_out, P1P0c0_out, P2G1_out, P2P1G0_out,
       P2P1P0c0_out;

  _4_bit_adder u_4_bit_adder_1 (
    .Carryin(CarryIn), .a0(a[0]), .a1(a[1]), .a2(a[2]), .a3(a[3]), .b0(b[0]), .b1(b[1]), .b2(b[2]),
    .b3(b[3]), .s0(SUM[0]), .s1(SUM[1]), .s2(SUM[2]), .s3(SUM[3]), .P0(n4_bit_adder_1_p0),
    .G0(n4_bit_adder_1_g0));  // open: Overflow
  _4_bit_adder u_4_bit_adder_2 (
    .Carryin(C1_out), .a0(a[4]), .a1(a[5]), .a2(a[6]), .a3(a[7]), .b0(b[4]), .b1(b[5]), .b2(b[6]), .b3(b[7]),
    .s0(SUM[4]), .s1(SUM[5]), .s2(SUM[6]), .s3(SUM[7]), .P0(n4_bit_adder_2_p0), .G0(n4_bit_adder_2_g0));  // open: Overflow
  _4_bit_adder u_4_bit_adder_3 (
    .Carryin(C2_out), .a0(a[8]), .a1(a[9]), .a2(a[10]), .a3(a[11]), .b0(b[8]), .b1(b[9]), .b2(b[10]),
    .b3(b[11]), .s0(SUM[8]), .s1(SUM[9]), .s2(SUM[10]), .s3(SUM[11]), .P0(n4_bit_adder_3_p0),
    .G0(n4_bit_adder_3_g0));  // open: Overflow
  _4_bit_adder u_4_bit_adder_4 (
    .Carryin(C3_out), .a0(a[12]), .a1(a[13]), .a2(a[14]), .a3(a[15]), .b0(b[12]), .b1(b[13]), .b2(b[14]),
    .b3(b[15]), .s0(SUM[12]), .s1(SUM[13]), .s2(SUM[14]), .s3(SUM[15]), .Overflow(Overflow));  // open: P0, G0
  and P2G1 (P2G1_out, n4_bit_adder_3_p0, n4_bit_adder_2_g0);
  and P2P1G0 (P2P1G0_out, n4_bit_adder_3_p0, n4_bit_adder_2_p0, n4_bit_adder_1_g0);
  and P2P1P0c0 (P2P1P0c0_out, n4_bit_adder_3_p0, n4_bit_adder_2_p0, n4_bit_adder_1_p0, CarryIn);
  and P0c0 (P0c0_out, CarryIn, n4_bit_adder_1_p0);
  and P1G0 (P1G0_out, n4_bit_adder_2_p0, n4_bit_adder_1_g0);
  and P1P0c0 (P1P0c0_out, n4_bit_adder_2_p0, n4_bit_adder_1_p0, CarryIn);
  or C1 (C1_out, P0c0_out, n4_bit_adder_1_g0);
  or C2 (C2_out, P1G0_out, P1P0c0_out, n4_bit_adder_2_g0);
  or C3 (C3_out, P2G1_out, P2P1G0_out, P2P1P0c0_out, n4_bit_adder_3_g0);
endmodule

module _4__Comparing (
  input  CarryIn,
  input  [15:0] a,
  input  [15:0] b,
  input  [15:0] a_2,
  input  [15:0] b_2,
  output [15:0] out_6,
  output Overflow,
  output [15:0] out_8,
  output Overflow_2
);

  Ripple_Carry_Adder ripple_carry (.Cin(CarryIn), .A(a), .B(b), .SUM(out_6), .out_5(Overflow));
  _12_bit_adder_carry_lookahead carry_Lookahead (
    .CarryIn(CarryIn), .a(a_2), .b(b_2), .SUM(out_8), .Overflow(Overflow_2));
endmodule
