// Logisim project ALU_LorekJeremi.circ as structural Verilog: 18 circuits, main circuit main
module main (
  output halt,
  output [12:0] counter,
  output [3:0] op,
  output [15:0] a,
  output [15:0] b,
  output [15:0] oracle,
  output [15:0] result,
  output err_oracle,
  output error,
  output ok,
  output start_delimiter
);

  wire and_1_out, and_2_out, clock_1_out, comparator_1_eq, comparator_2_eq;

  Clock clock_1 (.out(clock_1_out));
  Counter #(.width(13), .max('h1fff), .trigger("falling")) counter_1 (
    .Q(counter), .carry(halt), .clk(clock_1_out));  // open: load, D, count, clr
  RAM #(.addrWidth(16), .dataWidth(4), .bus("separate")) ram_1 (
    .addr({counter, 3'b000}), .data(op), .ld(1'b1));  // open: din, str, sel, clk, clr
  RAM #(.addrWidth(16), .dataWidth(16), .bus("separate")) ram_2 (
    .addr({counter, 3'b001}), .data(a), .ld(1'b1));  // open: din, str, sel, clk, clr
  RAM #(.addrWidth(16), .dataWidth(16), .bus("separate")) ram_3 (
    .addr({counter, 3'b010}), .data(b), .ld(1'b1));  // open: din, str, sel, clk, clr
  RAM #(.addrWidth(16), .dataWidth(16), .bus("separate")) ram_4 (
    .addr({counter, 3'b011}), .data(oracle), .ld(1'b1));  // open: din, str, sel, clk, clr
  RAM #(.addrWidth(16), .dataWidth(1), .bus("separate")) ram_5 (
    .addr({counter, 3'b100}), .data(err_oracle), .ld(1'b1));  // open: din, str, sel, clk, clr
  RAM #(.addrWidth(16), .dataWidth(1), .bus("separate")) ram_6 (
    .addr({counter, 3'b101}), .data(start_delimiter), .ld(1'b1));  // open: din, str, sel, clk, clr
  _16_bit_ALU u_16_bit_alu_1 (.ALU_code(op), .a(a), .b(b), .overflow(error), .result(result));
  Comparator #(.width(1), .mode("unsigned")) comparator_1 (
    .a(error), .b(err_oracle), .eq(comparator_1_eq));  // open: gt, lt
  Comparator #(.width(16)) comparator_2 (.a(result), .b(oracle), .eq(comparator_2_eq));  // open: gt, lt
  and and_1 (and_1_out, comparator_1_eq, error);
  and and_2 (and_2_out, comparator_2_eq, comparator_1_eq, ~error);  // AND_Gate
  or or_1 (ok, and_1_out, and_2_out);

  // Notes on the sheet:
  //   You must complete the circuit '16-bit ALU' instead.
  //   DO NOT EDIT THIS CIRCUIT!
endmodule

module _16_bit_ALU (
  input  [3:0] ALU_code,
  input  [15:0] a,
  input  [15:0] b,
  output [15:0] result,
  output overflow
);

  wire add_overflow, inv_overflow, sla_overflow, sub_overflow;
  wire [15:0] add_o, and_o, eq_o, gt_o, inv_o, lt_o, neq_o, noop_out_2, not_o, or_o, sla_out_2, sll_b, sra_o,
       srl_b, sub_o, zero_out_1;

  zero zero (.out_1(zero_out_1));
  \not  \not  (.a(a), .o(not_o));
  \and  \and  (.a(a), .b(b), .o(and_o));
  \or  \or  (.a(a), .b(b), .o(or_o));
  add add (.a(a), .b(b), .o(add_o), .Overflow(add_overflow));
  sub sub (.a(a), .b(b), .o(sub_o), .Overflow(sub_overflow));
  lt lt (.a(a), .b(b), .o(lt_o));
  gt gt (.a(a), .b(b), .o(gt_o));
  eq eq (.a(a), .b(b), .o(eq_o));
  neq neq (.a(a), .b(b), .o(neq_o));
  inv inv (.a(a), .o(inv_o), .Overflow(inv_overflow));
  sll sll (.a(a), .b(sll_b));
  srl srl (.a(a), .b(srl_b));
  sla sla (.a(a), .out_2(sla_out_2), .Overflow(sla_overflow));
  sra sra (.a(a), .o(sra_o));
  noop noop (.in_1(a), .out_2(noop_out_2));
  Multiplexer #(.select(4), .width(16)) multiplexer_1 (
    .in0(zero_out_1), .in1(not_o), .in2(and_o), .in3(or_o), .in4(add_o), .in5(sub_o), .in6(lt_o), .in7(gt_o),
    .in8(eq_o), .in9(neq_o), .in10(inv_o), .in11(sll_b), .in12(srl_b), .in13(sla_out_2), .in14(sra_o),
    .in15(noop_out_2), .out(result), .sel(ALU_code));  // open: en
  Multiplexer #(.select(4)) multiplexer_2 (
    .in0(1'b0), .in1(1'b0), .in2(1'b0), .in3(1'b0), .in4(add_overflow), .in5(sub_overflow), .in6(1'b0),
    .in7(1'b0), .in8(1'b0), .in9(1'b0), .in10(inv_overflow), .in11(1'b0), .in12(1'b0), .in13(sla_overflow),
    .in14(1'b0), .in15(1'b0), .out(overflow), .sel(ALU_code));  // open: en

  // Notes on the sheet:
  //   This circuit is used as a block in the main circuit, and its layout must remain unchanged. The circuit called "main" should be the main circuit of this file.
  //   Do not change the circuit appearance.
  //   DO NOT CHANGE THE INPUTS AND OUTPUTS OF THIS CIRCUIT!
  //   Do not add/remove inputs or outputs. Do not even change their location or orientation.
endmodule

module zero (
  output [15:0] out_1
);


  assign out_1 = {16{1'b0}};
endmodule

module \not  (
  input  [15:0] a,
  output [15:0] o
);

  assign o = ~a;  // NOT_Gate not_1, 16 bits wide
endmodule

module \and  (
  input  [15:0] a,
  input  [15:0] b,
  output [15:0] o
);

  assign o = a & b;  // AND_Gate and_1, 16 bits wide
endmodule

module \or  (
  input  [15:0] a,
  input  [15:0] b,
  output [15:0] o
);

  assign o = a | b;  // OR_Gate or_1, 16 bits wide
endmodule

module add (
  input  [15:0] a,
  input  [15:0] b,
  output [15:0] o,
  output Overflow
);

  _12_bit_adder_carry_lookahead u_12_bit_adder_carry_lookahead_1 (
    .CarryIn(1'b0), .a(a), .b(b), .SUM(o), .Overflow(Overflow));
endmodule

module sub (
  input  [15:0] a,
  input  [15:0] b,
  output [15:0] o,
  output Overflow
);

  wire [15:0] not_1_out;

  assign not_1_out = ~b;  // NOT_Gate not_1, 16 bits wide
  _12_bit_adder_carry_lookahead u_12_bit_adder_carry_lookahead_1 (
    .CarryIn(1'b1), .a(a), .b(not_1_out), .SUM(o), .Overflow(Overflow));
endmodule

module lt (
  input  [15:0] a,
  input  [15:0] b,
  output [15:0] o
);

  wire n12_bit_adder_carry_lookahead_1_overflow;
  wire [15:0] n12_bit_adder_carry_lookahead_1_sum, not_1_out;

  assign not_1_out = ~b;  // NOT_Gate not_1, 16 bits wide
  _12_bit_adder_carry_lookahead u_12_bit_adder_carry_lookahead_1 (
    .CarryIn(1'b1), .a(a), .b(not_1_out), .SUM(n12_bit_adder_carry_lookahead_1_sum),
    .Overflow(n12_bit_adder_carry_lookahead_1_overflow));
  xor xor_1 (o[0], n12_bit_adder_carry_lookahead_1_sum[15], n12_bit_adder_carry_lookahead_1_overflow);

  assign o[15:1] = {15{1'b0}};
endmodule

module gt (
  input  [15:0] a,
  input  [15:0] b,
  output [15:0] o
);

  wire n12_bit_adder_carry_lookahead_1_overflow;
  wire [15:0] n12_bit_adder_carry_lookahead_1_sum, not_1_out;

  assign not_1_out = ~a;  // NOT_Gate not_1, 16 bits wide
  _12_bit_adder_carry_lookahead u_12_bit_adder_carry_lookahead_1 (
    .CarryIn(1'b1), .a(not_1_out), .b(b), .SUM(n12_bit_adder_carry_lookahead_1_sum),
    .Overflow(n12_bit_adder_carry_lookahead_1_overflow));
  xor xor_1 (o[0], n12_bit_adder_carry_lookahead_1_sum[15], n12_bit_adder_carry_lookahead_1_overflow);

  assign o[15:1] = {15{1'b0}};
endmodule

module eq (
  input  [15:0] a,
  input  [15:0] b,
  output [15:0] o
);

  wire xnor_1_out, xnor_2_out, xnor_3_out, xnor_4_out, xnor_5_out, xnor_6_out, xnor_7_out, xnor_8_out,
       xnor_9_out, xnor_10_out, xnor_11_out, xnor_12_out, xnor_13_out, xnor_14_out, xnor_15_out, xnor_16_out;

  xnor xnor_1 (xnor_1_out, a[15], b[15]);
  xnor xnor_2 (xnor_2_out, a[14], b[14]);
  xnor xnor_3 (xnor_3_out, a[12], b[12]);
  xnor xnor_4 (xnor_4_out, a[13], b[13]);
  xnor xnor_5 (xnor_5_out, a[11], b[11]);
  xnor xnor_6 (xnor_6_out, a[10], b[10]);
  and and_1 (o[0], xnor_13_out, xnor_15_out, xnor_1_out, xnor_2_out, xnor_4_out, xnor_3_out, xnor_5_out, xnor_6_out, xnor_8_out, xnor_7_out, xnor_9_out, xnor_10_out, xnor_11_out, xnor_12_out, xnor_14_out, xnor_16_out);
  xnor xnor_7 (xnor_7_out, a[8], b[8]);
  xnor xnor_8 (xnor_8_out, a[9], b[9]);
  xnor xnor_9 (xnor_9_out, a[7], b[7]);
  xnor xnor_10 (xnor_10_out, a[6], b[6]);
  xnor xnor_11 (xnor_11_out, a[5], b[5]);
  xnor xnor_12 (xnor_12_out, a[4], b[4]);
  xnor xnor_13 (xnor_13_out, b[3], a[3]);
  xnor xnor_14 (xnor_14_out, b[1], a[1]);
  xnor xnor_15 (xnor_15_out, b[2], a[2]);
  xnor xnor_16 (xnor_16_out, b[0], a[0]);

  assign o[15:1] = {15{1'b0}};
endmodule

module neq (
  input  [15:0] a,
  input  [15:0] b,
  output [15:0] o
);

  wire and_1_out, xnor_1_out, xnor_2_out, xnor_3_out, xnor_4_out, xnor_5_out, xnor_6_out, xnor_7_out,
       xnor_8_out, xnor_9_out, xnor_10_out, xnor_11_out, xnor_12_out, xnor_13_out, xnor_14_out, xnor_15_out,
       xnor_16_out;

  xnor xnor_1 (xnor_1_out, a[14], b[14]);
  xnor xnor_2 (xnor_2_out, a[15], b[15]);
  xnor xnor_3 (xnor_3_out, a[12], b[12]);
  xnor xnor_4 (xnor_4_out, a[13], b[13]);
  xnor xnor_5 (xnor_5_out, a[11], b[11]);
  xnor xnor_6 (xnor_6_out, a[10], b[10]);
  and and_1 (and_1_out, xnor_13_out, xnor_15_out, xnor_2_out, xnor_1_out, xnor_4_out, xnor_3_out, xnor_5_out, xnor_6_out, xnor_7_out, xnor_8_out, xnor_9_out, xnor_10_out, xnor_12_out, xnor_11_out, xnor_14_out, xnor_16_out);
  not not_1 (o[0], and_1_out);
  xnor xnor_7 (xnor_7_out, a[9], b[9]);
  xnor xnor_8 (xnor_8_out, a[8], b[8]);
  xnor xnor_9 (xnor_9_out, a[7], b[7]);
  xnor xnor_10 (xnor_10_out, a[6], b[6]);
  xnor xnor_11 (xnor_11_out, a[4], b[4]);
  xnor xnor_12 (xnor_12_out, a[5], b[5]);
  xnor xnor_13 (xnor_13_out, b[3], a[3]);
  xnor xnor_14 (xnor_14_out, b[1], a[1]);
  xnor xnor_15 (xnor_15_out, b[2], a[2]);
  xnor xnor_16 (xnor_16_out, b[0], a[0]);

  assign o[15:1] = {15{1'b0}};
endmodule

module inv (
  input  [15:0] a,
  output [15:0] o,
  output Overflow
);

  wire [15:0] not_1_out;

  assign not_1_out = ~a;  // NOT_Gate not_1, 16 bits wide
  _12_bit_adder_carry_lookahead u_12_bit_adder_carry_lookahead_1 (
    .CarryIn(1'b0), .a(not_1_out), .b(16'h1), .SUM(o), .Overflow(Overflow));
endmodule

module sll (
  input  [15:0] a,
  output [15:0] b
);


  assign b = {a[14:0], 1'b0};
endmodule

module srl (
  input  [15:0] a,
  output [15:0] b
);


  assign b = {1'b0, a[15:1]};
endmodule

module sla (
  input  [15:0] a,
  output [15:0] out_2,
  output Overflow
);

  _12_bit_adder_carry_lookahead u_12_bit_adder_carry_lookahead_1 (
    .CarryIn(1'b0), .a(a), .b(a), .SUM(out_2), .Overflow(Overflow));
endmodule

module sra (
  input  [15:0] a,
  output [15:0] o
);

  and and_1 (o[15], a[15], 1'b1);

  assign o[14:0] = a[15:1];
endmodule

module noop (
  input  [15:0] in_1,
  output [15:0] out_2
);


  assign out_2 = in_1;
endmodule
