// Logisim project CSA 4.circ as structural Verilog: 4 circuits, main circuit 12 bit register
module _12_bit_register (
  input  C,
  input  [15:0] in_2,
  input  Write,
  input  Reset,
  output [15:0] Q
);

  D_Flip_Flop #(.trigger("falling")) d_ff_1 (
    .clk(C), .D(in_2[0]), .Q(Q[0]), .en(Write), .reset(Reset));  // open: Qn, preset
  D_Flip_Flop #(.trigger("falling")) d_ff_2 (
    .clk(C), .D(in_2[1]), .Q(Q[1]), .en(Write), .reset(Reset));  // open: Qn, preset
  D_Flip_Flop #(.trigger("falling")) d_ff_3 (
    .clk(C), .D(in_2[2]), .Q(Q[2]), .en(Write), .reset(Reset));  // open: Qn, preset
  D_Flip_Flop #(.trigger("falling")) d_ff_4 (
    .clk(C), .D(in_2[3]), .Q(Q[3]), .en(Write), .reset(Reset));  // open: Qn, preset
  D_Flip_Flop #(.trigger("falling")) d_ff_5 (
    .clk(C), .D(in_2[4]), .Q(Q[4]), .en(Write), .reset(Reset));  // open: Qn, preset
  D_Flip_Flop #(.trigger("falling")) d_ff_6 (
    .clk(C), .D(in_2[5]), .Q(Q[5]), .en(Write), .reset(Reset));  // open: Qn, preset
  D_Flip_Flop #(.trigger("falling")) d_ff_7 (
    .clk(C), .D(in_2[6]), .Q(Q[6]), .en(Write), .reset(Reset));  // open: Qn, preset
  D_Flip_Flop #(.trigger("falling")) d_ff_8 (
    .clk(C), .D(in_2[7]), .Q(Q[7]), .en(Write), .reset(Reset));  // open: Qn, preset
  D_Flip_Flop #(.trigger("falling")) d_ff_9 (
    .clk(C), .D(in_2[8]), .Q(Q[8]), .en(Write), .reset(Reset));  // open: Qn, preset
  D_Flip_Flop #(.trigger("falling")) d_ff_10 (
    .clk(C), .D(in_2[9]), .Q(Q[9]), .en(Write), .reset(Reset));  // open: Qn, preset
  D_Flip_Flop #(.trigger("falling")) d_ff_11 (
    .clk(C), .D(in_2[10]), .Q(Q[10]), .en(Write), .reset(Reset));  // open: Qn, preset
  D_Flip_Flop #(.trigger("falling")) d_ff_12 (
    .clk(C), .D(in_2[11]), .Q(Q[11]), .en(Write), .reset(Reset));  // open: Qn, preset
  D_Flip_Flop #(.trigger("falling")) d_ff_13 (
    .clk(C), .D(in_2[12]), .Q(Q[12]), .en(Write), .reset(Reset));  // open: Qn, preset
  D_Flip_Flop #(.trigger("falling")) d_ff_14 (
    .clk(C), .D(in_2[13]), .Q(Q[13]), .en(Write), .reset(Reset));  // open: Qn, preset
  D_Flip_Flop #(.trigger("falling")) d_ff_15 (
    .clk(C), .D(in_2[14]), .Q(Q[14]), .en(Write), .reset(Reset));  // open: Qn, preset
  D_Flip_Flop #(.trigger("falling")) d_ff_16 (
    .clk(C), .D(in_2[15]), .Q(Q[15]), .en(Write), .reset(Reset));  // open: Qn, preset
endmodule

module register_file (
  input  [2:0] rs,
  input  [2:0] rt,
  input  Clock,
  input  [15:0] Data,
  input  Write,
  input  [2:0] rd,
  input  Reset,
  output [15:0] S,
  output [15:0] T
);

  wire and_1_out, and_2_out, and_3_out, and_4_out, and_5_out, and_6_out, and_7_out, decoder_1_out1,
       decoder_1_out2, decoder_1_out3, decoder_1_out4, decoder_1_out5, decoder_1_out6, decoder_1_out7;
  wire [15:0] n12_bit_register_1_q, n12_bit_register_2_q, n12_bit_register_3_q, n12_bit_register_4_q,
       n12_bit_register_5_q, n12_bit_register_6_q, n12_bit_register_7_q, n12_bit_register_8_q;

  Decoder #(.select(3), .disabled(0)) decoder_1 (
    .out1(decoder_1_out1), .out2(decoder_1_out2), .out3(decoder_1_out3), .out4(decoder_1_out4),
    .out5(decoder_1_out5), .out6(decoder_1_out6), .out7(decoder_1_out7), .sel(rd));  // open: out0, en
  and and_1 (and_1_out, decoder_1_out1, Write);
  and and_2 (and_2_out, decoder_1_out2, Write);
  and and_3 (and_3_out, decoder_1_out3, Write);
  and and_4 (and_4_out, decoder_1_out4, Write);
  and and_5 (and_5_out, decoder_1_out5, Write);
  and and_6 (and_6_out, decoder_1_out6, Write);
  and and_7 (and_7_out, decoder_1_out7, Write);
  _12_bit_register u_12_bit_register_1 (
    .C(Clock), .in_2({16{1'b0}}), .Write(1'b0), .Reset(Reset), .Q(n12_bit_register_1_q));
  _12_bit_register u_12_bit_register_2 (
    .C(Clock), .in_2(Data), .Write(and_1_out), .Reset(Reset), .Q(n12_bit_register_2_q));
  _12_bit_register u_12_bit_register_3 (
    .C(Clock), .in_2(Data), .Write(and_2_out), .Reset(Reset), .Q(n12_bit_register_3_q));
  _12_bit_register u_12_bit_register_4 (
    .C(Clock), .in_2(Data), .Write(and_3_out), .Reset(Reset), .Q(n12_bit_register_4_q));
  _12_bit_register u_12_bit_register_5 (
    .C(Clock), .in_2(Data), .Write(and_4_out), .Reset(Reset), .Q(n12_bit_register_5_q));
  _12_bit_register u_12_bit_register_6 (
    .C(Clock), .in_2(Data), .Write(and_5_out), .Reset(Reset), .Q(n12_bit_register_6_q));
  _12_bit_register u_12_bit_register_7 (
    .C(Clock), .in_2(Data), .Write(and_6_out), .Reset(Reset), .Q(n12_bit_register_7_q));
  _12_bit_register u_12_bit_register_8 (
    .C(Clock), .in_2(Data), .Write(and_7_out), .Reset(Reset), .Q(n12_bit_register_8_q));
  Multiplexer #(.select(3), .width(16)) multiplexer_1 (
    .in0(n12_bit_register_1_q), .in1(n12_bit_register_2_q), .in2(n12_bit_register_3_q),
    .in3(n12_bit_register_4_q), .in4(n12_bit_register_5_q), .in5(n12_bit_register_6_q),
    .in6(n12_bit_register_7_q), .in7(n12_bit_register_8_q), .out(S), .sel(rs));  // open: en
  Multiplexer #(.select(3), .width(16)) multiplexer_2 (
    .in0(n12_bit_register_1_q), .in1(n12_bit_register_2_q), .in2(n12_bit_register_3_q),
    .in3(n12_bit_register_4_q), .in4(n12_bit_register_5_q), .in5(n12_bit_register_6_q),
    .in6(n12_bit_register_7_q), .in7(n12_bit_register_8_q), .out(T), .sel(rt));  // open: en
endmodule

module counter (
  input  Clock,
  input  [15:0] in_2,
  output [15:0] out_3
);

  wire comparator_1_eq, comparator_1_gt, comparator_1_lt, or_1_out;
  wire [15:0] n12_bit_adder_carry_lookahead_1_sum;

  _12_bit_adder_carry_lookahead u_12_bit_adder_carry_lookahead_1 (
    .CarryIn(1'b1), .a(out_3), .b({16{1'b0}}), .SUM(n12_bit_adder_carry_lookahead_1_sum));  // open: Overflow
  Comparator #(.width(16)) comparator_1 (
    .a(out_3), .b(in_2), .gt(comparator_1_gt), .eq(comparator_1_eq), .lt(comparator_1_lt));
  _12_bit_register u_12_bit_register_1 (
    .C(Clock), .in_2(n12_bit_adder_carry_lookahead_1_sum), .Write(comparator_1_lt), .Reset(or_1_out),
    .Q(out_3));
  or or_1 (or_1_out, comparator_1_gt, comparator_1_eq);
endmodule

module traffic_light (
);

  wire and_1_out, and_2_out, and_3_out, clock_1_out, comparator_1_eq, comparator_1_gt, comparator_1_lt,
       comparator_2_eq, comparator_2_gt, comparator_2_lt, comparator_3_eq, comparator_3_gt, comparator_3_lt,
       comparator_4_eq, comparator_4_gt, comparator_4_lt, comparator_5_eq, comparator_5_gt, comparator_5_lt,
       or_1_out, or_2_out, or_3_out, or_4_out;
  wire [15:0] counter_1_out_3;

  // Probe on counter_1_out_3
  Comparator #(.width(16)) comparator_1 (
    .a(counter_1_out_3), .b(16'hb), .gt(comparator_1_gt), .eq(comparator_1_eq), .lt(comparator_1_lt));
  Comparator #(.width(16)) comparator_2 (
    .a(counter_1_out_3), .b(16'h8), .gt(comparator_2_gt), .eq(comparator_2_eq), .lt(comparator_2_lt));
  and and_1 (and_1_out, comparator_1_lt, comparator_2_gt);
  LED led_1 (.in(comparator_1_gt));
  or or_1 (or_1_out, comparator_1_eq, and_1_out, comparator_2_eq);
  LED led_2 (.in(or_1_out));
  LED led_3 (.in(comparator_2_lt));
  counter counter_1 (.in_2(16'h1c), .out_3(counter_1_out_3), .Clock(clock_1_out));
  Clock clock_1 (.out(clock_1_out));
  Comparator #(.width(16)) comparator_3 (
    .a(counter_1_out_3), .b(16'he), .gt(comparator_3_gt), .eq(comparator_3_eq), .lt(comparator_3_lt));
  Comparator #(.width(16)) comparator_4 (
    .a(counter_1_out_3), .b(16'h19), .gt(comparator_4_gt), .eq(comparator_4_eq), .lt(comparator_4_lt));
  Comparator #(.width(16)) comparator_5 (
    .a(counter_1_out_3), .b(16'h16), .gt(comparator_5_gt), .eq(comparator_5_eq), .lt(comparator_5_lt));
  or or_2 (or_2_out, comparator_3_lt, comparator_4_gt);
  and and_2 (and_2_out, comparator_3_gt, comparator_5_lt);
  LED led_4 (.in(or_2_out));
  LED led_5 (.in(or_3_out));
  or or_3 (or_3_out, comparator_4_eq, and_3_out, comparator_5_eq);
  or or_4 (or_4_out, comparator_3_eq, and_2_out);
  LED led_6 (.in(or_4_out));
  and and_3 (and_3_out, comparator_4_lt, comparator_5_gt);
endmodule
