// Logisim project FD_Group65.circ as structural Verilog: 7 circuits, main circuit main
module main (
  output [11:0] pc,
  output [11:0] r0,
  output [11:0] r1,
  output [11:0] r2,
  output [11:0] r3,
  output [11:0] r4,
  output [11:0] r5,
  output [11:0] r6,
  output [11:0] r7,
  output halt
);

  wire and_1_out, and_2_out, bit_extender_2_out, clock_1_out, comparator_1_eq, controller_1_alusrc,
       controller_1_beq, controller_1_blt, controller_1_j, controller_1_jal, controller_1_jr,
       controller_1_memread, controller_1_memtoreg, controller_1_memwrite, controller_1_regwrite, or_1_out,
       or_2_out, or_3_out, reset_out;
  wire [2:0] decoder_1_rd, decoder_1_rs, decoder_1_rt, multiplexer_3_out, multiplexer_5_out;
  wire [3:0] controller_1_aluop, decoder_1_function_code, decoder_1_operation_code;
  wire [7:0] decoder_1_target_adress;
  wire [11:0] bit_extender_1_out, decoder_1_immediate, multiplexer_1_out, multiplexer_2_out,
       multiplexer_4_out, multiplexer_6_out, multiplexer_7_out, multiplexer_8_out, multiplexer_9_out,
       multiplexer_10_out, multiplexer_11_out, n12_bit_alu_1_result, Programm_counter_pc___1, ram_2_data,
       register_file_modified_1_s, register_file_modified_1_t;
  wire [15:0] ram_1_data;

  Halt halt_1 (.instruction(ram_1_data), .clock(clock_1_out), .reset(reset_out), .halt(halt));
  Clock clock_1 (.out(clock_1_out));
  Button reset (.out(reset_out));
  Multiplexer #(.width(12)) multiplexer_1 (
    .in0(bit_extender_1_out), .in1(n12_bit_alu_1_result), .out(multiplexer_1_out), .sel(controller_1_jr));  // open: en
  and and_1 (and_1_out, ~halt, clock_1_out);  // AND_Gate
  Multiplexer #(.width(12)) multiplexer_2 (
    .in0(multiplexer_1_out), .in1(decoder_1_immediate), .out(multiplexer_2_out), .sel(and_2_out));  // open: en
  Program_Counter Programm_counter (
    .Branch_relative(and_2_out), .Branch_absolute(or_1_out), .branch_value(multiplexer_2_out), .C(and_1_out),
    .reset(reset_out), .Instruction_adress(pc), .PC___1(Programm_counter_pc___1));
  RAM #(.addrWidth(12), .dataWidth(16)) ram_1 (
    .addr(pc), .data(ram_1_data), .clk(and_1_out), .ld(1'b1), .clr(reset_out));  // open: sel
  assign bit_extender_1_out = {{4{1'b0}}, decoder_1_target_adress};  // Bit_Extender bit_extender_1
  Multiplexer #(.width(3)) multiplexer_3 (
    .in0(decoder_1_rt), .in1(decoder_1_rd), .out(multiplexer_3_out), .sel(controller_1_memwrite));  // open: en
  Multiplexer #(.width(12)) multiplexer_4 (
    .in0(multiplexer_11_out), .in1(Programm_counter_pc___1), .out(multiplexer_4_out), .sel(controller_1_jal));  // open: en
  Multiplexer #(.width(3)) multiplexer_5 (
    .in0(decoder_1_rd), .in1(3'b111), .out(multiplexer_5_out), .sel(controller_1_jal));  // open: en
  Decoder decoder_1 (
    .rt(decoder_1_rt), .rs(decoder_1_rs), .rd(decoder_1_rd), .Instruction(ram_1_data),
    .Immediate(decoder_1_immediate), .Operation_Code(decoder_1_operation_code),
    .Function_code(decoder_1_function_code), .Target_Adress(decoder_1_target_adress));
  or or_1 (or_1_out, controller_1_jal, controller_1_j, controller_1_jr);
  Register_File___Modified register_file_modified_1 (
    .rs(decoder_1_rs), .rt(multiplexer_3_out), .Clock(and_1_out), .Data(multiplexer_4_out),
    .Write(controller_1_regwrite), .rd(multiplexer_5_out), .Reset(reset_out), .S(register_file_modified_1_s),
    .T(register_file_modified_1_t), .r0(r0), .r1(r1), .r2(r2), .r3(r3), .r4(r4), .r5(r5), .r6(r6), .r7(r7));
  controller controller_1 (
    .Operation_code(decoder_1_operation_code), .Function_code(decoder_1_function_code),
    .ALUop(controller_1_aluop), .ALUsrc(controller_1_alusrc), .MemToReg(controller_1_memtoreg),
    .MemRead(controller_1_memread), .MemWrite(controller_1_memwrite), .jr(controller_1_jr),
    .j(controller_1_j), .jal(controller_1_jal), .beq(controller_1_beq), .blt(controller_1_blt),
    .RegWrite(controller_1_regwrite));
  Multiplexer #(.width(12)) multiplexer_6 (
    .in0(register_file_modified_1_t), .in1(decoder_1_immediate), .out(multiplexer_6_out),
    .sel(controller_1_alusrc));  // open: en
  Multiplexer #(.width(12)) multiplexer_7 (
    .in0(register_file_modified_1_s), .in1({12{1'b0}}), .out(multiplexer_7_out), .sel(comparator_1_eq));  // open: en
  Multiplexer #(.select(3), .width(12)) multiplexer_8 (
    .in0(r0), .in1(r1), .in2(r2), .in3(r3), .in4(r4), .in5(r5), .in6(r6), .in7(r7), .out(multiplexer_8_out),
    .sel(decoder_1_rd));  // open: en
  Comparator #(.width(4), .mode("unsigned")) comparator_1 (
    .a(decoder_1_operation_code), .b(4'b1100), .eq(comparator_1_eq));  // open: gt, lt
  or or_2 (or_2_out, controller_1_jr, controller_1_beq, controller_1_blt);
  or or_3 (or_3_out, controller_1_beq, controller_1_blt);
  Multiplexer #(.width(12)) multiplexer_9 (
    .in0(multiplexer_7_out), .in1(multiplexer_8_out), .out(multiplexer_9_out), .sel(or_2_out));  // open: en
  Multiplexer #(.width(12)) multiplexer_10 (
    .in0(multiplexer_6_out), .in1(register_file_modified_1_s), .out(multiplexer_10_out), .sel(or_3_out));  // open: en
  _12_bit_ALU u_12_bit_alu_1 (
    .ALU_code(controller_1_aluop), .a(multiplexer_9_out), .b(multiplexer_10_out),
    .result(n12_bit_alu_1_result));  // open: overflow
  and and_2 (and_2_out, or_3_out, bit_extender_2_out);
  Bit_Extender #(.in_width(12), .out_width(1)) bit_extender_2 (.in(n12_bit_alu_1_result), .out(bit_extender_2_out));
  RAM #(.addrWidth(12), .dataWidth(12), .bus("separate")) ram_2 (
    .addr(n12_bit_alu_1_result), .din(register_file_modified_1_t), .data(ram_2_data),
    .str(controller_1_memwrite), .clk(and_1_out), .ld(controller_1_memread), .clr(reset_out));  // open: sel
  Multiplexer #(.width(12)) multiplexer_11 (
    .in0(n12_bit_alu_1_result), .in1(ram_2_data), .out(multiplexer_11_out), .sel(controller_1_memtoreg));  // open: en

  // Notes on the sheet:
  //   current instruction
  //   clock signal
  //   reset button
  //   DO NOT CHANGE THE INPUTS AND OUTPUTS OF THIS CIRCUIT! Do not add/remove inputs or outputs. Do not even change their location or orientation.
endmodule

module Halt (
  input  [15:0] instruction,
  input  clock,
  input  reset,
  output halt
);

  wire and_1_out, comparator_1_eq, comparator_2_gt, counter_1_carry, or_1_out, or_2_out;
  wire [11:0] counter_1_q;

  Comparator #(.width(16), .mode("unsigned")) comparator_1 (
    .a(instruction), .b({16{1'b0}}), .eq(comparator_1_eq));  // open: gt, lt
  Counter #(.width(12), .max('hfff), .trigger("falling")) counter_1 (
    .Q(counter_1_q), .carry(counter_1_carry), .clk(clock), .clr(reset));  // open: load, D, count
  or or_1 (or_1_out, comparator_1_eq, counter_1_carry);
  Comparator #(.width(12), .mode("unsigned")) comparator_2 (
    .a(counter_1_q), .b({12{1'b0}}), .gt(comparator_2_gt));  // open: eq, lt
  or or_2 (or_2_out, halt, and_1_out);
  and and_1 (and_1_out, or_1_out, comparator_2_gt);
  Register #(.width(1)) register_1 (.D(or_2_out), .Q(halt), .clk(clock), .clr(reset));  // open: en

  // Notes on the sheet:
  //   halt becomes and stays asserted if the instruction is 0000 (not in the first clock cycle) or the end of the counter is reached (2^12)
endmodule

module Program_Counter (
  input  Branch_relative,
  input  Branch_absolute,
  input  [11:0] branch_value,
  input  C,
  input  reset,
  output [11:0] PC___1,
  output [11:0] Instruction_adress
);

  wire [11:0] adder_2_out, multiplexer_1_out, multiplexer_2_out;

  Adder #(.width(12)) adder_1 (.a(Instruction_adress), .b(12'h1), .out(PC___1));  // open: cin, cout
  Multiplexer #(.width(12)) multiplexer_1 (
    .in0(PC___1), .in1(adder_2_out), .out(multiplexer_1_out), .sel(Branch_relative));  // open: en
  Adder #(.width(12)) adder_2 (.a(PC___1), .b(branch_value), .out(adder_2_out));  // open: cin, cout
  Multiplexer #(.width(12)) multiplexer_2 (
    .in0(multiplexer_1_out), .in1(branch_value), .out(multiplexer_2_out), .sel(Branch_absolute));  // open: en
  _12_bit_register u_12_bit_register_1 (
    .C(C), .in_2(multiplexer_2_out), .Write(1'b1), .Reset(reset), .Q(Instruction_adress));
endmodule

module Decoder (
  input  [15:0] Instruction,
  output [2:0] rt,
  output [2:0] rs,
  output [2:0] rd,
  output [11:0] Immediate,
  output [3:0] Operation_Code,
  output [3:0] Function_code,
  output [7:0] Target_Adress
);

  wire and_1_out, and_2_out, and_3_out, and_4_out, comparator_1_eq, comparator_1_gt, comparator_1_lt,
       comparator_2_eq, comparator_2_gt, comparator_2_lt, comparator_3_eq, comparator_4_eq, comparator_5_eq,
       comparator_6_eq, comparator_7_eq, comparator_8_eq, comparator_8_gt, comparator_9_eq, comparator_9_lt,
       comparator_10_eq, comparator_11_eq, comparator_12_eq, comparator_13_eq, comparator_14_eq, or_1_out,
       or_2_out, or_3_out, or_4_out, or_5_out, or_6_out;
  wire [2:0] multiplexer_11_out;
  wire [3:0] multiplexer_1_out, multiplexer_2_out, multiplexer_4_out, multiplexer_6_out, multiplexer_7_out;
  wire [7:0] multiplexer_3_out;
  wire [11:0] bit_extender_1_out, bit_extender_3_out, bit_extender_5_out, bit_extender_6_out,
       bit_extender_7_out, multiplexer_17_out, multiplexer_18_out, multiplexer_20_out;

  Comparator #(.width(4), .mode("unsigned")) comparator_1 (
    .a(Instruction[15:12]), .b(4'b0001), .gt(comparator_1_gt), .eq(comparator_1_eq), .lt(comparator_1_lt));
  Comparator #(.width(4), .mode("unsigned")) comparator_2 (
    .a(Instruction[15:12]), .b(4'b1010), .gt(comparator_2_gt), .eq(comparator_2_eq), .lt(comparator_2_lt));
  Comparator #(.width(4), .mode("unsigned")) comparator_3 (
    .a(Instruction[15:12]), .b(4'b1011), .eq(comparator_3_eq));  // open: gt, lt
  Comparator #(.width(4), .mode("unsigned")) comparator_4 (
    .a(Instruction[15:12]), .b(4'b1100), .eq(comparator_4_eq));  // open: gt, lt
  Comparator #(.width(4), .mode("unsigned")) comparator_5 (
    .a(Instruction[15:12]), .b(4'b1101), .eq(comparator_5_eq));  // open: gt, lt
  Comparator #(.width(4), .mode("unsigned")) comparator_6 (
    .a(Instruction[15:12]), .b(4'b1110), .eq(comparator_6_eq));  // open: gt, lt
  Comparator #(.width(4), .mode("unsigned")) comparator_7 (
    .a(Instruction[15:12]), .b(4'b1111), .eq(comparator_7_eq));  // open: gt, lt
  Comparator comparator_8 (
    .a(Instruction[7:0]), .b({Instruction[7:4], 4'b0001}), .gt(comparator_8_gt), .eq(comparator_8_eq));  // open: lt
  Comparator comparator_9 (
    .a(Instruction[7:0]), .b({Instruction[7:4], 4'b1111}), .eq(comparator_9_eq), .lt(comparator_9_lt));  // open: gt
  and and_1 (and_1_out, comparator_1_gt, comparator_2_lt);
  Multiplexer #(.width(4)) multiplexer_1 (
    .in1(Instruction[3:0]), .out(multiplexer_1_out), .sel(comparator_2_eq));  // open: in0, en
  Multiplexer #(.width(4)) multiplexer_2 (
    .in1(Instruction[3:0]), .out(multiplexer_2_out), .sel(comparator_3_eq));  // open: in0, en
  Multiplexer #(.width(8)) multiplexer_3 (
    .in1(Instruction[7:0]), .out(multiplexer_3_out), .sel(comparator_4_eq));  // open: in0, en
  Multiplexer #(.width(4)) multiplexer_4 (
    .in1(Instruction[3:0]), .out(multiplexer_4_out), .sel(comparator_5_eq));  // open: in0, en
  Multiplexer #(.width(4)) multiplexer_5 (
    .in1(Instruction[3:0]), .out(Function_code), .sel(comparator_1_eq));  // open: in0, en
  or or_1 (or_1_out, comparator_2_eq, comparator_2_gt);
  Multiplexer #(.width(4)) multiplexer_6 (
    .in1(Instruction[3:0]), .out(multiplexer_6_out), .sel(comparator_6_eq));  // open: in0, en
  assign bit_extender_1_out = {{8{multiplexer_6_out[3]}}, multiplexer_6_out};  // Bit_Extender bit_extender_1
  assign bit_extender_1_out = {{8{multiplexer_7_out[3]}}, multiplexer_7_out};  // Bit_Extender bit_extender_2
  Multiplexer #(.width(4)) multiplexer_7 (
    .in1(Instruction[3:0]), .out(multiplexer_7_out), .sel(comparator_7_eq));  // open: in0, en
  and and_2 (and_2_out, comparator_9_lt, or_2_out);
  or or_2 (or_2_out, comparator_8_gt, comparator_8_eq);
  assign bit_extender_3_out = {{8{1'b0}}, multiplexer_1_out};  // Bit_Extender bit_extender_3
  assign bit_extender_3_out = {{8{1'b0}}, multiplexer_2_out};  // Bit_Extender bit_extender_4
  assign bit_extender_5_out = {{4{multiplexer_3_out[7]}}, multiplexer_3_out};  // Bit_Extender bit_extender_5
  assign bit_extender_6_out = {{8{multiplexer_4_out[3]}}, multiplexer_4_out};  // Bit_Extender bit_extender_6
  Multiplexer #(.width(4)) multiplexer_8 (.in1(4'b0000), .out(Function_code), .sel(comparator_1_lt));  // open: in0, en
  Multiplexer #(.width(4)) multiplexer_9 (
    .in1(Instruction[15:12]), .out(Function_code), .sel(and_1_out));  // open: in0, en
  Multiplexer #(.width(4)) multiplexer_10 (.in1(4'b0100), .out(Function_code), .sel(or_1_out));  // open: in0, en
  or or_3 (or_3_out, comparator_6_eq, comparator_7_eq);
  or or_4 (or_4_out, comparator_9_eq, and_2_out);
  Multiplexer #(.width(3)) multiplexer_11 (
    .in1(Instruction[6:4]), .out(multiplexer_11_out), .sel(or_4_out));  // open: in0, en
  Multiplexer #(.width(3)) multiplexer_12 (.in1(Instruction[2:0]), .out(rt), .sel(and_1_out));  // open: in0, en
  Multiplexer #(.width(3)) multiplexer_13 (
    .in1(Instruction[6:4]), .out(multiplexer_11_out), .sel(and_1_out));  // open: in0, en
  Multiplexer #(.width(3)) multiplexer_14 (
    .in1(Instruction[6:4]), .out(multiplexer_11_out), .sel(or_5_out));  // open: in0, en
  or or_5 (or_5_out, comparator_2_eq, comparator_3_eq, comparator_5_eq);
  Comparator #(.width(4)) comparator_10 (.a(Function_code), .b(4'b0010), .eq(comparator_10_eq));  // open: gt, lt
  and and_3 (and_3_out, comparator_1_eq, comparator_10_eq);
  Multiplexer #(.width(3)) multiplexer_15 (.in0(multiplexer_11_out), .out(rs), .sel(and_3_out));  // open: in1, en
  Multiplexer #(.width(3)) multiplexer_16 (.in0(Instruction[10:8]), .out(rd), .sel(and_4_out));  // open: in1, en
  and and_4 (and_4_out, comparator_1_eq, or_6_out);
  Comparator #(.width(4)) comparator_11 (.a(Function_code), .b(4'b0011), .eq(comparator_11_eq));  // open: gt, lt
  Comparator #(.width(4)) comparator_12 (.a(Function_code), .b(4'b0100), .eq(comparator_12_eq));  // open: gt, lt
  Multiplexer #(.width(12)) multiplexer_17 (
    .in0(bit_extender_3_out), .in1(bit_extender_6_out), .out(multiplexer_17_out), .sel(comparator_13_eq));  // open: en
  or or_6 (or_6_out, comparator_11_eq, comparator_12_eq);
  Multiplexer #(.width(12)) multiplexer_18 (
    .in0(multiplexer_17_out), .in1(bit_extender_5_out), .out(multiplexer_18_out), .sel(comparator_14_eq));  // open: en
  Comparator #(.width(4)) comparator_13 (.a(Instruction[15:12]), .b(4'b1101), .eq(comparator_13_eq));  // open: gt, lt
  Multiplexer #(.width(8)) multiplexer_19 (
    .in1(Instruction[11:4]), .out(Target_Adress), .sel(and_4_out));  // open: in0, en
  Comparator #(.width(4)) comparator_14 (.a(Instruction[15:12]), .b(4'b1100), .eq(comparator_14_eq));  // open: gt, lt
  Multiplexer #(.width(12)) multiplexer_20 (
    .in0(multiplexer_18_out), .in1(bit_extender_7_out), .out(multiplexer_20_out), .sel(and_3_out));  // open: en
  assign bit_extender_7_out = {{8{Instruction[7]}}, Instruction[7:4]};  // Bit_Extender bit_extender_7
  Multiplexer #(.width(12)) multiplexer_21 (
    .in0(multiplexer_20_out), .in1(bit_extender_1_out), .out(Immediate), .sel(or_3_out));  // open: en

  assign Operation_Code = Instruction[15:12];
endmodule

module controller (
  input  [3:0] Operation_code,
  input  [3:0] Function_code,
  output [3:0] ALUop,
  output ALUsrc,
  output MemToReg,
  output MemRead,
  output MemWrite,
  output jr,
  output j,
  output jal,
  output beq,
  output blt,
  output RegWrite
);

  wire ADD_out, ADDI_out, and_1_out, AND_2_out, CP_out, EQ_out, GT_out, INV_out, LDI_out, LT_out, NEQ_out,
       not_1_out, not_2_out, not_3_out, not_4_out, not_5_out, not_6_out, not_7_out, not_8_out, NOT_9_out,
       or_5_out, OR_out, SLA_out, SLL_out, SRA_out, SRL_out, SUB_out;

  not not_1 (not_1_out, Operation_code[0]);
  not not_2 (not_2_out, Operation_code[1]);
  not not_3 (not_3_out, Operation_code[2]);
  not not_4 (not_4_out, Operation_code[3]);
  and and_1 (and_1_out, not_4_out, not_3_out, not_2_out, Operation_code[0]);
  not not_5 (not_5_out, Function_code[0]);
  not not_6 (not_6_out, Function_code[1]);
  not not_7 (not_7_out, Function_code[2]);
  not not_8 (not_8_out, Function_code[3]);
  // AND_Gate zero has open pins: in0=not_4_out, in1=not_3_out, in2=not_2_out, in3=not_1_out, out=open
  and AND_2 (AND_2_out, not_1_out, Operation_code[1], not_3_out, not_4_out);
  and OR (OR_out, Operation_code[0], Operation_code[1], not_3_out, not_4_out);
  and ADD (ADD_out, not_1_out, not_2_out, Operation_code[2], not_4_out);
  and SUB (SUB_out, Operation_code[0], not_2_out, Operation_code[2], not_4_out);
  and LT (LT_out, not_1_out, Operation_code[1], Operation_code[2], not_4_out);
  and GT (GT_out, Operation_code[0], Operation_code[1], Operation_code[2], not_4_out);
  and EQ (EQ_out, not_1_out, not_2_out, not_3_out, Operation_code[3]);
  and NEQ (NEQ_out, Operation_code[0], not_2_out, not_3_out, Operation_code[3]);
  and LW (MemRead, not_1_out, Operation_code[1], not_3_out, Operation_code[3]);
  and SW (MemWrite, Operation_code[0], Operation_code[1], not_3_out, Operation_code[3]);
  and LDI (LDI_out, not_1_out, not_2_out, Operation_code[2], Operation_code[3]);
  and ADDI (ADDI_out, Operation_code[0], not_2_out, Operation_code[2], Operation_code[3]);
  and u_BEQ (beq, not_1_out, Operation_code[1], Operation_code[2], Operation_code[3]);
  and u_BLT (blt, Operation_code[0], Operation_code[1], Operation_code[2], Operation_code[3]);
  and NOT_9 (NOT_9_out, Function_code[0], not_6_out, and_1_out, not_7_out, not_8_out);
  and INV (INV_out, not_5_out, Function_code[1], and_1_out, not_7_out, Function_code[3]);
  and SLL (SLL_out, Function_code[0], Function_code[1], and_1_out, not_7_out, Function_code[3]);
  and SRL (SRL_out, not_5_out, not_6_out, and_1_out, Function_code[2], Function_code[3]);
  and SLA (SLA_out, Function_code[0], not_6_out, and_1_out, Function_code[2], Function_code[3]);
  and SRA (SRA_out, not_5_out, Function_code[1], and_1_out, Function_code[2], Function_code[3]);
  and CP (CP_out, Function_code[0], Function_code[1], and_1_out, Function_code[2], Function_code[3]);
  and u_JR (jr, not_5_out, Function_code[1], and_1_out, not_7_out, not_8_out);
  and u_J (j, Function_code[0], Function_code[1], and_1_out, not_7_out, not_8_out);
  and u_JAL (jal, not_5_out, not_6_out, and_1_out, Function_code[2], not_8_out);
  or or_2 (ALUop[1], MemWrite, AND_2_out, OR_out, LT_out, GT_out, INV_out, SLL_out, SRA_out, CP_out, blt);
  or or_3 (ALUop[3], MemWrite, EQ_out, NEQ_out, INV_out, SLL_out, SRL_out, SLA_out, SRA_out, CP_out, beq);
  or or_4 (ALUop[0], OR_out, SUB_out, GT_out, NEQ_out, MemWrite, NOT_9_out, SLL_out, SLA_out, CP_out);
  or or_5 (or_5_out, beq, jr, MemWrite, j, blt);
  not not_10 (RegWrite, or_5_out);
  or or_6 (ALUop[2], blt, MemRead, MemWrite, ADD_out, SUB_out, LT_out, GT_out, SRL_out, SLA_out, SRA_out, CP_out, LDI_out, ADDI_out, jal, jr);
  or or_7 (ALUsrc, MemRead, jr, MemWrite, ADDI_out, LDI_out);

  assign MemToReg = MemRead;
endmodule

module Register_File___Modified (
  input  [2:0] rs,
  input  [2:0] rt,
  input  Clock,
  input  [11:0] Data,
  input  Write,
  input  [2:0] rd,
  input  Reset,
  output [11:0] S,
  output [11:0] T,
  output [11:0] r0,
  output [11:0] r1,
  output [11:0] r2,
  output [11:0] r3,
  output [11:0] r4,
  output [11:0] r5,
  output [11:0] r6,
  output [11:0] r7
);

  wire and_1_out, and_2_out, and_3_out, and_4_out, and_5_out, and_6_out, and_7_out, decoder_1_out1,
       decoder_1_out2, decoder_1_out3, decoder_1_out4, decoder_1_out5, decoder_1_out6, decoder_1_out7;

  Decoder_part #(.select(3), .disabled(0)) decoder_1 (
    .out1(decoder_1_out1), .out2(decoder_1_out2), .out3(decoder_1_out3), .out4(decoder_1_out4),
    .out5(decoder_1_out5), .out6(decoder_1_out6), .out7(decoder_1_out7), .sel(rd));  // open: out0, en
  and and_1 (and_1_out, decoder_1_out1, Write);
  and and_2 (and_2_out, decoder_1_out2, Write);
  and and_3 (and_3_out, decoder_1_out3, Write);
  and and_4 (and_4_out, decoder_1_out4, Write);
  and and_5 (and_5_out, decoder_1_out5, Write);
  and and_6 (and_6_out, decoder_1_out6, Write);
  and and_7 (and_7_out, decoder_1_out7, Write);
  _12_bit_register u_12_bit_register_1 (.C(Clock), .in_2({12{1'b0}}), .Write(1'b0), .Reset(Reset), .Q(r0));
  _12_bit_register u_12_bit_register_2 (.C(Clock), .in_2(Data), .Write(and_1_out), .Reset(Reset), .Q(r1));
  _12_bit_register u_12_bit_register_3 (.C(Clock), .in_2(Data), .Write(and_2_out), .Reset(Reset), .Q(r2));
  _12_bit_register u_12_bit_register_4 (.C(Clock), .in_2(Data), .Write(and_3_out), .Reset(Reset), .Q(r3));
  _12_bit_register u_12_bit_register_5 (.C(Clock), .in_2(Data), .Write(and_4_out), .Reset(Reset), .Q(r4));
  _12_bit_register u_12_bit_register_6 (.C(Clock), .in_2(Data), .Write(and_5_out), .Reset(Reset), .Q(r5));
  _12_bit_register u_12_bit_register_7 (.C(Clock), .in_2(Data), .Write(and_6_out), .Reset(Reset), .Q(r6));
  _12_bit_register u_12_bit_register_8 (.C(Clock), .in_2(Data), .Write(and_7_out), .Reset(Reset), .Q(r7));
  Multiplexer #(.select(3), .width(12)) multiplexer_1 (
    .in0(r0), .in1(r1), .in2(r2), .in3(r3), .in4(r4), .in5(r5), .in6(r6), .in7(r7), .out(S), .sel(rs));  // open: en
  Multiplexer #(.select(3), .width(12)) multiplexer_2 (
    .in0(r0), .in1(r1), .in2(r2), .in3(r3), .in4(r4), .in5(r5), .in6(r6), .in7(r7), .out(T), .sel(rt));  // open: en
endmodule

module pc_test (
  input  in_1,
  input  in_2,
  input  [11:0] in_3,
  input  in_4,
  output [11:0] out_5
);

  wire clock_1_out;

  Clock clock_1 (.out(clock_1_out));
  Program_Counter program_counter_1 (
    .Branch_relative(in_1), .Branch_absolute(in_2), .branch_value(in_3), .C(clock_1_out), .reset(in_4),
    .Instruction_adress(out_5));  // open: PC___1
endmodule
