// Logisim project CSA 1.circ as structural Verilog: 3 circuits, main circuit exercise 3
module exercise_3 (
  input  A,
  input  A_2,
  input  B,
  input  A_3,
  input  B_2,
  output X,
  output X_2,
  output x_3
);

  wire nand_2_out, nand_3_out, nand_4_out;

  nand nand_1 (X, A, A);
  nand nand_2 (nand_2_out, A_2, B);
  nand nand_3 (nand_3_out, A_3, A_3);
  nand nand_4 (nand_4_out, B_2, B_2);
  nand nand_5 (X_2, nand_2_out, nand_2_out);
  nand nand_6 (x_3, nand_3_out, nand_4_out);

  // Notes on the sheet:
  //   = NOT GATE
  //   = AND GATE
  //   = OR GATE
endmodule

module exercise_4 (
  input  A,
  input  B,
  input  C,
  output X,
  output Y
);

  wire and_1_out, and_2_out, and_3_out, and_4_out, and_5_out, not_1_out, not_2_out, not_3_out;

  not not_1 (not_1_out, A);
  not not_2 (not_2_out, B);
  not not_3 (not_3_out, C);
  and and_1 (and_1_out, not_1_out, not_2_out, not_3_out);
  and and_2 (and_2_out, not_1_out, not_2_out, C);
  and and_3 (and_3_out, not_1_out, B, not_3_out);
  and and_4 (and_4_out, A, B, not_3_out);
  and and_5 (and_5_out, A, not_2_out, not_3_out);
  or or_1 (X, and_5_out, and_2_out, and_1_out);
  or or_2 (Y, and_4_out, and_5_out, and_3_out, and_2_out, and_1_out);
endmodule

module exercise_5 (
  input  [2:0] in_1
);

  wire a_out, and_1_out, and_2_out, and_3_out, and_4_out, and_5_out, and_6_out, and_7_out, and_8_out,
       and_9_out, and_10_out, and_11_out, and_12_out, and_13_out, and_14_out, and_15_out, and_16_out,
       and_17_out, and_18_out, b_out, d_out, e_out, f_out, g_out, not_1_out, not_2_out, not_3_out, not_4_out,
       not_5_out, not_6_out, not_7_out, not_8_out, not_9_out;

  or a (a_out, and_1_out, and_2_out);
  not not_1 (not_1_out, a_out);
  or b (b_out, and_3_out, and_4_out);
  not not_2 (not_2_out, b_out);
  not not_3 (not_3_out, in_1[0]);
  not not_4 (not_4_out, in_1[1]);
  not not_5 (not_5_out, in_1[2]);
  and and_1 (and_1_out, not_5_out, not_4_out, in_1[0]);
  not not_6 (not_6_out, and_5_out);
  and and_2 (and_2_out, in_1[2], not_4_out, not_3_out);
  or d (d_out, and_6_out, and_7_out, and_8_out);
  or e (e_out, and_9_out, and_10_out, and_12_out);
  not not_7 (not_7_out, d_out);
  _7_Segment_Display u_7_segment_display_1 (
    .g(not_9_out), .f(not_8_out), .a(not_1_out), .b(not_2_out), .e(e_out), .d(not_7_out), .c(not_6_out));  // open: dp
  and and_3 (and_3_out, in_1[2], not_4_out, in_1[0]);
  and and_4 (and_4_out, in_1[2], in_1[1], not_3_out);
  or f (f_out, and_11_out, and_13_out, and_14_out, and_15_out);
  not not_8 (not_8_out, f_out);
  and and_5 (and_5_out, not_5_out, in_1[1], not_3_out);
  or g (g_out, and_16_out, and_17_out, and_18_out);
  not not_9 (not_9_out, g_out);
  and and_6 (and_6_out, not_5_out, not_4_out, in_1[0]);
  and and_7 (and_7_out, in_1[2], not_4_out, not_3_out);
  and and_8 (and_8_out, in_1[2], in_1[1], in_1[0]);
  and and_9 (and_9_out, not_5_out, not_4_out, not_3_out);
  and and_10 (and_10_out, not_5_out, in_1[1], not_3_out);
  and and_11 (and_11_out, not_5_out, not_4_out, in_1[0]);
  and and_12 (and_12_out, in_1[2], in_1[1], not_3_out);
  and and_13 (and_13_out, not_5_out, in_1[1], not_3_out);
  and and_14 (and_14_out, not_5_out, in_1[1], in_1[0]);
  and and_15 (and_15_out, in_1[2], in_1[1], in_1[0]);
  and and_16 (and_16_out, not_5_out, not_4_out, not_3_out);
  and and_17 (and_17_out, not_5_out, not_4_out, in_1[0]);
  and and_18 (and_18_out, in_1[2], in_1[1], in_1[0]);
endmodule
