// Logisim project ALU_Group65.circ as structural Verilog: 18 circuits, main circuit main
module main (
  output halt,
  output [12:0] counter,
  output [3:0] op,
  output [11:0] a,
  output [11:0] b,
  output [11:0] oracle,
  output [11:0] result,
  output err_oracle,
  output error,
  output ok,
  output start_delimiter
);

  wire and_1_out, and_2_out, clock_1_out, comparator_1_eq, comparator_2_eq;

  Clock clock_1 (.out(clock_1_out));
  Counter #(.width(13), .max('h1fff), .trigger("falling")) counter_1 (
    .Q(counter), .carry(halt), .clk(clock_1_out));  // open: load, D, count, clr
  RAM #(.addrWidth(16), .dataWidth(4), .bus("separate")) ram_1 (
    .addr({counter, 3'b000}), .data(op), .ld(1'b1));  // open: din, str, sel, clk, clr
  RAM #(.addrWidth(16), .dataWidth(12), .bus("separate")) ram_2 (
    .addr({counter, 3'b001}), .data(a), .ld(1'b1));  // open: din, str, sel, clk, clr
  RAM #(.addrWidth(16), .dataWidth(12), .bus("separate")) ram_3 (
    .addr({counter, 3'b010}), .data(b), .ld(1'b1));  // open: din, str, sel, clk, clr
  RAM #(.addrWidth(16), .dataWidth(12), .bus("separate")) ram_4 (
    .addr({counter, 3'b011}), .data(oracle), .ld(1'b1));  // open: din, str, sel, clk, clr
  RAM #(.addrWidth(16), .dataWidth(1), .bus("separate")) ram_5 (
    .addr({counter, 3'b100}), .data(err_oracle), .ld(1'b1));  // open: din, str, sel, clk, clr
  RAM #(.addrWidth(16), .dataWidth(1), .bus("separate")) ram_6 (
    .addr({counter, 3'b101}), .data(start_delimiter), .ld(1'b1));  // open: din, str, sel, clk, clr
  _12_bit_ALU u_12_bit_alu_1 (.ALU_code(op), .a(a), .b(b), .overflow(error), .result(result));
  Comparator #(.width(1), .mode("unsigned")) comparator_1 (
    .a(error), .b(err_oracle), .eq(comparator_1_eq));  // open: gt, lt
  Comparator #(.width(12)) comparator_2 (.a(result), .b(oracle), .eq(comparator_2_eq));  // open: gt, lt
  and and_1 (and_1_out, comparator_1_eq, error);
  and and_2 (and_2_out, comparator_2_eq, comparator_1_eq, ~error);  // AND_Gate
  or or_1 (ok, and_1_out, and_2_out);

  // Notes on the sheet:
  //   You must complete the circuit '12-bit ALU' instead.
  //   DO NOT EDIT THIS CIRCUIT!
endmodule

module _12_bit_ALU (
  input  [3:0] ALU_code,
  input  [11:0] a,
  input  [11:0] b,
  output [11:0] result,
  output overflow
);

  wire add_overflow, inv_overflow, sla_overflow, sub_overflow;
  wire [11:0] add_o, and_o, eq_o, gt_o, inv_o, lt_o, neq_o, noop_o, not_o, or_o, sla_out_2, sll_out_2, sra_o,
       srl_o, sub_o, zero_out_1;

  zero zero (.out_1(zero_out_1));
  \not  \not  (.a(a), .o(not_o));
  \and  \and  (.a(a), .b(b), .o(and_o));
  \or  \or  (.a(a), .b(b), .o(or_o));
  add add (.a(a), .b(b), .o(add_o), .Overflow(add_overflow));
  sub sub (.a(a), .b(b), .o(sub_o), .Overflow(sub_overflow));
  lt lt (.a(a), .b(b), .o(lt_o));
  gt gt (.a(a), .b(b), .o(gt_o));
  eq eq (.a(a), .b(b), .o(eq_o));
  neq neq (.a(a), .b(b), .o(neq_o));
  inv inv (.a(a), .o(inv_o), .Overflow(inv_overflow));
  sll sll (.a(a), .out_2(sll_out_2));
  srl srl (.a(a), .o(srl_o));
  sla sla (.a(a), .out_2(sla_out_2), .Overflow(sla_overflow));
  sra sra (.a(a), .o(sra_o));
  noop noop (.a(a), .o(noop_o));
  Multiplexer #(.select(4), .width(12)) multiplexer_1 (
    .in0(zero_out_1), .in1(not_o), .in2(and_o), .in3(or_o), .in4(add_o), .in5(sub_o), .in6(lt_o), .in7(gt_o),
    .in8(eq_o), .in9(neq_o), .in10(inv_o), .in11(sll_out_2), .in12(srl_o), .in13(sla_out_2), .in14(sra_o),
    .in15(noop_o), .out(result), .sel(ALU_code));  // open: en
  Multiplexer #(.select(4)) multiplexer_2 (
    .in0(1'b0), .in1(1'b0), .in2(1'b0), .in3(1'b0), .in4(add_overflow), .in5(sub_overflow), .in6(1'b0),
    .in7(1'b0), .in8(1'b0), .in9(1'b0), .in10(inv_overflow), .in11(1'b0), .in12(1'b0), .in13(sla_overflow),
    .in14(1'b0), .in15(1'b0), .out(overflow), .sel(ALU_code));  // open: en

  // Notes on the sheet:
  //   This circuit is used as a block in the main circuit, and its layout must remain unchanged. The circuit called "main" should be the main circuit of this file.
  //   Do not change the circuit appearance.
  //   DO NOT CHANGE THE INPUTS AND OUTPUTS OF THIS CIRCUIT!
  //   Do not add/remove inputs or outputs. Do not even change their location or orientation.
endmodule

module zero (
  output [11:0] out_1
);


  assign out_1 = {12{1'b0}};
endmodule

module \not  (
  input  [11:0] a,
  output [11:0] o
);

  assign o = ~a;  // NOT_Gate not_1, 12 bits wide
endmodule

module \and  (
  input  [11:0] a,
  input  [11:0] b,
  output [11:0] o
);

  assign o = a & b;  // AND_Gate and_1, 12 bits wide
endmodule

module \or  (
  input  [11:0] a,
  input  [11:0] b,
  output [11:0] o
);

  assign o = a | b;  // OR_Gate or_1, 12 bits wide
endmodule

module add (
  input  [11:0] a,
  input  [11:0] b,
  output [11:0] o,
  output Overflow
);

  _12_bit_adder_carry_lookahead u_12_bit_adder_carry_lookahead_1 (
    .CarryIn(1'b0), .a(a), .b(b), .SUM(o), .Overflow(Overflow));
endmodule

module sub (
  input  [11:0] a,
  input  [11:0] b,
  output [11:0] o,
  output Overflow
);

  wire [11:0] not_1_out;

  assign not_1_out = ~b;  // NOT_Gate not_1, 12 bits wide
  _12_bit_adder_carry_lookahead u_12_bit_adder_carry_lookahead_1 (
    .CarryIn(1'b1), .a(a), .b(not_1_out), .SUM(o), .Overflow(Overflow));
endmodule

module lt (
  input  [11:0] a,
  input  [11:0] b,
  output [11:0] o
);

  wire n12_bit_adder_carry_lookahead_1_overflow;
  wire [11:0] n12_bit_adder_carry_lookahead_1_sum, not_1_out;

  assign not_1_out = ~b;  // NOT_Gate not_1, 12 bits wide
  _12_bit_adder_carry_lookahead u_12_bit_adder_carry_lookahead_1 (
    .CarryIn(1'b1), .a(a), .b(not_1_out), .SUM(n12_bit_adder_carry_lookahead_1_sum),
    .Overflow(n12_bit_adder_carry_lookahead_1_overflow));
  xor xor_1 (o[0], n12_bit_adder_carry_lookahead_1_sum[11], n12_bit_adder_carry_lookahead_1_overflow);

  assign o[11:1] = {11{1'b0}};
endmodule

module gt (
  input  [11:0] a,
  input  [11:0] b,
  output [11:0] o
);

  wire n12_bit_adder_carry_lookahead_1_overflow;
  wire [11:0] n12_bit_adder_carry_lookahead_1_sum, not_1_out;

  assign not_1_out = ~a;  // NOT_Gate not_1, 12 bits wide
  _12_bit_adder_carry_lookahead u_12_bit_adder_carry_lookahead_1 (
    .CarryIn(1'b1), .a(not_1_out), .b(b), .SUM(n12_bit_adder_carry_lookahead_1_sum),
    .Overflow(n12_bit_adder_carry_lookahead_1_overflow));
  xor xor_1 (o[0], n12_bit_adder_carry_lookahead_1_sum[11], n12_bit_adder_carry_lookahead_1_overflow);

  assign o[11:1] = {11{1'b0}};
endmodule

module eq (
  input  [11:0] a,
  input  [11:0] b,
  output [11:0] o
);

  wire xnor_1_out, xnor_2_out, xnor_3_out, xnor_4_out, xnor_5_out, xnor_6_out, xnor_7_out, xnor_8_out,
       xnor_9_out, xnor_10_out, xnor_11_out, xnor_12_out;

  xnor xnor_1 (xnor_1_out, a[11], b[11]);
  xnor xnor_2 (xnor_2_out, a[10], b[10]);
  xnor xnor_3 (xnor_3_out, a[9], b[9]);
  xnor xnor_4 (xnor_4_out, a[7], b[7]);
  xnor xnor_5 (xnor_5_out, a[8], b[8]);
  and and_1 (o[0], xnor_1_out, xnor_2_out, xnor_3_out, xnor_5_out, xnor_4_out, xnor_7_out, xnor_6_out, xnor_9_out, xnor_8_out, xnor_11_out, xnor_10_out, xnor_12_out);
  xnor xnor_6 (xnor_6_out, a[5], b[5]);
  xnor xnor_7 (xnor_7_out, a[6], b[6]);
  xnor xnor_8 (xnor_8_out, a[3], b[3]);
  xnor xnor_9 (xnor_9_out, a[4], b[4]);
  xnor xnor_10 (xnor_10_out, a[1], b[1]);
  xnor xnor_11 (xnor_11_out, a[2], b[2]);
  xnor xnor_12 (xnor_12_out, a[0], b[0]);

  assign o[11:1] = {11{1'b0}};
endmodule

module neq (
  input  [11:0] a,
  input  [11:0] b,
  output [11:0] o
);

  wire and_1_out, xnor_1_out, xnor_2_out, xnor_3_out, xnor_4_out, xnor_5_out, xnor_6_out, xnor_7_out,
       xnor_8_out, xnor_9_out, xnor_10_out, xnor_11_out, xnor_12_out;

  xnor xnor_1 (xnor_1_out, a[11], b[11]);
  xnor xnor_2 (xnor_2_out, a[9], b[9]);
  xnor xnor_3 (xnor_3_out, a[10], b[10]);
  xnor xnor_4 (xnor_4_out, a[7], b[7]);
  xnor xnor_5 (xnor_5_out, a[8], b[8]);
  and and_1 (and_1_out, xnor_1_out, xnor_3_out, xnor_2_out, xnor_5_out, xnor_4_out, xnor_6_out, xnor_7_out, xnor_9_out, xnor_8_out, xnor_11_out, xnor_10_out, xnor_12_out);
  not not_1 (o[0], and_1_out);
  xnor xnor_6 (xnor_6_out, a[6], b[6]);
  xnor xnor_7 (xnor_7_out, a[5], b[5]);
  xnor xnor_8 (xnor_8_out, a[3], b[3]);
  xnor xnor_9 (xnor_9_out, a[4], b[4]);
  xnor xnor_10 (xnor_10_out, a[1], b[1]);
  xnor xnor_11 (xnor_11_out, a[2], b[2]);
  xnor xnor_12 (xnor_12_out, a[0], b[0]);

  assign o[11:1] = {11{1'b0}};
endmodule

module inv (
  input  [11:0] a,
  output [11:0] o,
  output Overflow
);

  wire [11:0] not_1_out;

  assign not_1_out = ~a;  // NOT_Gate not_1, 12 bits wide
  add add_1 (.a(not_1_out), .b(12'h1), .o(o), .Overflow(Overflow));
endmodule

module sll (
  input  [11:0] a,
  output [11:0] out_2
);


  assign out_2 = {a[10:0], 1'b0};
endmodule

module srl (
  input  [11:0] a,
  output [11:0] o
);


  assign o = {1'b0, a[11:1]};
endmodule

module sla (
  input  [11:0] a,
  output [11:0] out_2,
  output Overflow
);

  add add_1 (.a(a), .b(a), .o(out_2), .Overflow(Overflow));
endmodule

module sra (
  input  [11:0] a,
  output [11:0] o
);

  and and_1 (o[11], a[11], 1'b1);

  assign o[10:0] = a[11:1];
endmodule

module noop (
  input  [11:0] a,
  output [11:0] o
);


  assign o = a;
endmodule
