// Logisim project SD_Group65.circ as structural Verilog: 7 circuits, main circuit main
module main (
  output [11:0] pc,
  output [11:0] r0,
  output [11:0] r1,
  output [11:0] r2,
  output [11:0] r3,
  output [11:0] r4,
  output [11:0] r5,
  output [11:0] r6,
  output [11:0] r7,
  output halt
);

  wire and_1_out, clock_1_out, reset_out;
  wire [15:0] ram_1_data;

  Halt halt_1 (.instruction(ram_1_data), .clock(clock_1_out), .reset(reset_out), .halt(halt));
  Clock clock_1 (.out(clock_1_out));
  Button reset (.out(reset_out));
  and and_1 (and_1_out, ~halt, clock_1_out);  // AND_Gate
  RAM #(.addrWidth(12), .dataWidth(16)) ram_1 (
    .data(ram_1_data), .clk(and_1_out), .ld(1'b1), .clr(reset_out));  // open: addr, sel
  Register_File___Modified register_file_modified_1 (
    .Clock(and_1_out), .Reset(reset_out), .r0(r0), .r1(r1), .r2(r2), .r3(r3), .r4(r4), .r5(r5), .r6(r6),
    .r7(r7));  // open: rs, rt, Data, Write, rd, S, T

  // Notes on the sheet:
  //   current instruction
  //   clock signal
  //   reset button
  //   DO NOT CHANGE THE INPUTS AND OUTPUTS OF THIS CIRCUIT! Do not add/remove inputs or outputs. Do not even change their location or orientation.
endmodule

module Halt (
  input  [15:0] instruction,
  input  clock,
  input  reset,
  output halt
);

  wire and_1_out, comparator_1_eq, comparator_2_gt, counter_1_carry, or_1_out, or_2_out;
  wire [11:0] counter_1_q;

  Comparator #(.width(16), .mode("unsigned")) comparator_1 (
    .a(instruction), .b({16{1'b0}}), .eq(comparator_1_eq));  // open: gt, lt
  Counter #(.width(12), .max('hfff), .trigger("falling")) counter_1 (
    .Q(counter_1_q), .carry(counter_1_carry), .clk(clock), .clr(reset));  // open: load, D, count
  or or_1 (or_1_out, comparator_1_eq, counter_1_carry);
  Comparator #(.width(12), .mode("unsigned")) comparator_2 (
    .a(counter_1_q), .b({12{1'b0}}), .gt(comparator_2_gt));  // open: eq, lt
  or or_2 (or_2_out, halt, and_1_out);
  and and_1 (and_1_out, or_1_out, comparator_2_gt);
  Register #(.width(1)) register_1 (.D(or_2_out), .Q(halt), .clk(clock), .clr(reset));  // open: en

  // Notes on the sheet:
  //   halt becomes and stays asserted if the instruction is 0000 (not in the first clock cycle) or the end of the counter is reached (2^12)
endmodule

module Program_Counter (
  input  Branch_relative,
  input  Branch_absolute,
  input  [11:0] branch_value,
  input  C,
  input  reset,
  output [11:0] Instruction_adress
);

  wire [11:0] adder_1_out, adder_2_out, multiplexer_1_out, multiplexer_2_out;

  Adder #(.width(12)) adder_1 (.a(Instruction_adress), .b(12'h1), .out(adder_1_out));  // open: cin, cout
  Multiplexer #(.width(12)) multiplexer_1 (
    .in0(adder_1_out), .in1(adder_2_out), .out(multiplexer_1_out), .sel(Branch_relative));  // open: en
  Adder #(.width(12)) adder_2 (.a(adder_1_out), .b(branch_value), .out(adder_2_out));  // open: cin, cout
  Multiplexer #(.width(12)) multiplexer_2 (
    .in0(multiplexer_1_out), .in1(branch_value), .out(multiplexer_2_out), .sel(Branch_absolute));  // open: en
  _12_bit_register u_12_bit_register_1 (
    .C(C), .in_2(multiplexer_2_out), .Write(1'b1), .Reset(reset), .Q(Instruction_adress));
endmodule

module Decoder (
  input  [15:0] Instruction,
  output [2:0] rt,
  output [2:0] rs,
  output [2:0] rd,
  output [11:0] Immediate,
  output [3:0] Operation_Code,
  output [3:0] Function_code
);

  wire and_1_out, and_2_out, comparator_1_eq, comparator_1_gt, comparator_1_lt, comparator_2_eq,
       comparator_2_gt, comparator_2_lt, comparator_3_eq, comparator_4_eq, comparator_5_eq, comparator_6_eq,
       comparator_6_gt, comparator_7_eq, comparator_7_lt, or_1_out, or_2_out, or_3_out, or_4_out;
  wire [2:0] multiplexer_2_out, multiplexer_3_out, multiplexer_5_out;
  wire [5:0] multiplexer_4_out;

  Comparator #(.width(4), .mode("unsigned")) comparator_1 (
    .a(Instruction[15:12]), .b(4'b0001), .gt(comparator_1_gt), .eq(comparator_1_eq), .lt(comparator_1_lt));
  Comparator #(.width(4), .mode("unsigned")) comparator_2 (
    .a(Instruction[15:12]), .b(4'b1010), .gt(comparator_2_gt), .eq(comparator_2_eq), .lt(comparator_2_lt));
  Comparator #(.width(4), .mode("unsigned")) comparator_3 (
    .a(Instruction[15:12]), .b(4'b1011), .eq(comparator_3_eq));  // open: gt, lt
  Comparator #(.width(4), .mode("unsigned")) comparator_4 (
    .a(Instruction[15:12]), .b(4'b1100), .eq(comparator_4_eq));  // open: gt, lt
  Comparator #(.width(4), .mode("unsigned")) comparator_5 (
    .a(Instruction[15:12]), .b(4'b1101), .eq(comparator_5_eq));  // open: gt, lt
  Comparator comparator_6 (
    .a(Instruction[7:0]), .b({Instruction[7:4], 4'b0001}), .gt(comparator_6_gt), .eq(comparator_6_eq));  // open: lt
  and and_1 (and_1_out, comparator_1_gt, comparator_2_lt);
  Multiplexer #(.width(4)) multiplexer_1 (
    .in1(Instruction[3:0]), .out(Function_code), .sel(comparator_1_eq));  // open: in0, en
  or or_1 (or_1_out, comparator_2_eq, comparator_2_gt);
  Comparator comparator_7 (
    .a(Instruction[7:0]), .b({Instruction[7:4], 4'b1111}), .eq(comparator_7_eq), .lt(comparator_7_lt));  // open: gt
  or or_2 (or_2_out, comparator_6_gt, comparator_6_eq);
  Multiplexer #(.width(3)) multiplexer_2 (
    .in1(Instruction[2:0]), .out(multiplexer_2_out), .sel(comparator_2_eq));  // open: in0, en
  Multiplexer #(.width(3)) multiplexer_3 (
    .in1(Instruction[2:0]), .out(multiplexer_3_out), .sel(comparator_3_eq));  // open: in0, en
  Multiplexer #(.width(6)) multiplexer_4 (
    .in1({Instruction[10:8], Instruction[2:0]}), .out(multiplexer_4_out), .sel(comparator_4_eq));  // open: in0, en
  Multiplexer #(.width(3)) multiplexer_5 (
    .in1(Instruction[2:0]), .out(multiplexer_5_out), .sel(comparator_5_eq));  // open: in0, en
  Multiplexer #(.width(4)) multiplexer_6 (.in1(4'b0000), .out(Function_code), .sel(comparator_1_lt));  // open: in0, en
  and and_2 (and_2_out, comparator_7_lt, or_2_out);
  assign Immediate = {{9{1'b0}}, multiplexer_2_out};  // Bit_Extender bit_extender_1
  assign Immediate = {{9{1'b0}}, multiplexer_3_out};  // Bit_Extender bit_extender_2
  assign Immediate = {{6{1'b0}}, multiplexer_4_out};  // Bit_Extender bit_extender_3
  assign Immediate = {{9{1'b0}}, multiplexer_5_out};  // Bit_Extender bit_extender_4
  or or_3 (or_3_out, comparator_7_eq, and_2_out);
  Multiplexer #(.width(4)) multiplexer_7 (
    .in1(Instruction[15:12]), .out(Function_code), .sel(and_1_out));  // open: in0, en
  Multiplexer #(.width(3)) multiplexer_8 (.in1(Instruction[6:4]), .out(rs), .sel(or_3_out));  // open: in0, en
  Multiplexer #(.width(3)) multiplexer_9 (.in1(Instruction[2:0]), .out(rt), .sel(and_1_out));  // open: in0, en
  Multiplexer #(.width(3)) multiplexer_10 (.in1(Instruction[6:4]), .out(rs), .sel(and_1_out));  // open: in0, en
  Multiplexer #(.width(3)) multiplexer_11 (.in1(Instruction[6:4]), .out(rs), .sel(or_4_out));  // open: in0, en
  or or_4 (or_4_out, comparator_2_eq, comparator_3_eq, comparator_5_eq);

  assign Operation_Code = Instruction[15:12];
  assign rd = Instruction[10:8];
endmodule

module controller (
  input  [3:0] in_1,
  input  [3:0] in_2
);
endmodule

module Register_File___Modified (
  input  [2:0] rs,
  input  [2:0] rt,
  input  Clock,
  input  [11:0] Data,
  input  Write,
  input  [2:0] rd,
  input  Reset,
  output [11:0] S,
  output [11:0] T,
  output [11:0] r0,
  output [11:0] r1,
  output [11:0] r2,
  output [11:0] r3,
  output [11:0] r4,
  output [11:0] r5,
  output [11:0] r6,
  output [11:0] r7
);

  wire and_1_out, and_2_out, and_3_out, and_4_out, and_5_out, and_6_out, and_7_out, decoder_1_out1,
       decoder_1_out2, decoder_1_out3, decoder_1_out4, decoder_1_out5, decoder_1_out6, decoder_1_out7;

  Decoder_part #(.select(3), .disabled(0)) decoder_1 (
    .out1(decoder_1_out1), .out2(decoder_1_out2), .out3(decoder_1_out3), .out4(decoder_1_out4),
    .out5(decoder_1_out5), .out6(decoder_1_out6), .out7(decoder_1_out7), .sel(rd));  // open: out0, en
  and and_1 (and_1_out, decoder_1_out1, Write);
  and and_2 (and_2_out, decoder_1_out2, Write);
  and and_3 (and_3_out, decoder_1_out3, Write);
  and and_4 (and_4_out, decoder_1_out4, Write);
  and and_5 (and_5_out, decoder_1_out5, Write);
  and and_6 (and_6_out, decoder_1_out6, Write);
  and and_7 (and_7_out, decoder_1_out7, Write);
  _12_bit_register u_12_bit_register_1 (.C(Clock), .in_2({12{1'b0}}), .Write(1'b0), .Reset(Reset), .Q(r0));
  _12_bit_register u_12_bit_register_2 (.C(Clock), .in_2(Data), .Write(and_1_out), .Reset(Reset), .Q(r1));
  _12_bit_register u_12_bit_register_3 (.C(Clock), .in_2(Data), .Write(and_2_out), .Reset(Reset), .Q(r2));
  _12_bit_register u_12_bit_register_4 (.C(Clock), .in_2(Data), .Write(and_3_out), .Reset(Reset), .Q(r3));
  _12_bit_register u_12_bit_register_5 (.C(Clock), .in_2(Data), .Write(and_4_out), .Reset(Reset), .Q(r4));
  _12_bit_register u_12_bit_register_6 (.C(Clock), .in_2(Data), .Write(and_5_out), .Reset(Reset), .Q(r5));
  _12_bit_register u_12_bit_register_7 (.C(Clock), .in_2(Data), .Write(and_6_out), .Reset(Reset), .Q(r6));
  _12_bit_register u_12_bit_register_8 (.C(Clock), .in_2(Data), .Write(and_7_out), .Reset(Reset), .Q(r7));
  Multiplexer #(.select(3), .width(12)) multiplexer_1 (
    .in0(r0), .in1(r1), .in2(r2), .in3(r3), .in4(r4), .in5(r5), .in6(r6), .in7(r7), .out(S), .sel(rs));  // open: en
  Multiplexer #(.select(3), .width(12)) multiplexer_2 (
    .in0(r0), .in1(r1), .in2(r2), .in3(r3), .in4(r4), .in5(r5), .in6(r6), .in7(r7), .out(T), .sel(rt));  // open: en
endmodule

module pc_test (
  input  in_1,
  input  in_2,
  input  [11:0] in_3,
  input  in_4,
  output [11:0] out_5
);

  wire clock_1_out;

  Clock clock_1 (.out(clock_1_out));
  Program_Counter program_counter_1 (
    .Branch_relative(in_1), .Branch_absolute(in_2), .branch_value(in_3), .C(clock_1_out), .reset(in_4),
    .Instruction_adress(out_5));
endmodule
